// Logisim project adderTest.circ as structural Verilog: 4 circuits, main circuit main
module main (
  input  in_1,
  input  [31:0] A,
  input  [31:0] B,
  output out_4,
  output [31:0] SUM
);

  Base32Adder base32adder_1 (.CarryIn(in_1), .A(A), .B(B), .SUM(SUM), .CarryOut(out_4));
endmodule

module SingleBitAdder (
  input  A,
  input  B,
  input  CarryIn,
  output SUM,
  output CarryOut
);

  wire and_1_out, and_2_out, xor_1_out;

  xor xor_1 (xor_1_out, A, B);
  xor xor_2 (SUM, xor_1_out, CarryIn);
  and and_1 (and_1_out, CarryIn, xor_1_out);
  and and_2 (and_2_out, B, A);
  or or_1 (CarryOut, and_1_out, and_2_out);
endmodule

module OctalAdder (
  input  CarryIn,
  input  [7:0] A,
  input  [7:0] B,
  output CarryOut,
  output [7:0] SUM
);

  wire singlebitadder_1_carryout, singlebitadder_2_carryout, singlebitadder_3_carryout,
       singlebitadder_4_carryout, singlebitadder_5_carryout, singlebitadder_6_carryout,
       singlebitadder_7_carryout;

  SingleBitAdder singlebitadder_1 (
    .A(A[0]), .B(B[0]), .CarryIn(CarryIn), .SUM(SUM[0]), .CarryOut(singlebitadder_1_carryout));
  SingleBitAdder singlebitadder_2 (
    .A(A[1]), .B(B[1]), .CarryIn(singlebitadder_1_carryout), .SUM(SUM[1]),
    .CarryOut(singlebitadder_2_carryout));
  SingleBitAdder singlebitadder_3 (
    .A(A[2]), .B(B[2]), .CarryIn(singlebitadder_2_carryout), .SUM(SUM[2]),
    .CarryOut(singlebitadder_3_carryout));
  SingleBitAdder singlebitadder_4 (
    .A(A[3]), .B(B[3]), .CarryIn(singlebitadder_3_carryout), .SUM(SUM[3]),
    .CarryOut(singlebitadder_4_carryout));
  SingleBitAdder singlebitadder_5 (
    .A(A[4]), .B(B[4]), .CarryIn(singlebitadder_4_carryout), .SUM(SUM[4]),
    .CarryOut(singlebitadder_5_carryout));
  SingleBitAdder singlebitadder_6 (
    .A(A[5]), .B(B[5]), .CarryIn(singlebitadder_5_carryout), .SUM(SUM[5]),
    .CarryOut(singlebitadder_6_carryout));
  SingleBitAdder singlebitadder_7 (
    .A(A[6]), .B(B[6]), .CarryIn(singlebitadder_6_carryout), .SUM(SUM[6]),
    .CarryOut(singlebitadder_7_carryout));
  SingleBitAdder singlebitadder_8 (
    .A(A[7]), .B(B[7]), .CarryIn(singlebitadder_7_carryout), .SUM(SUM[7]), .CarryOut(CarryOut));
endmodule

module Base32Adder (
  input  CarryIn,
  input  [31:0] A,
  input  [31:0] B,
  output [31:0] SUM,
  output CarryOut
);

  wire octaladder_1_carryout, octaladder_2_carryout, octaladder_3_carryout;

  OctalAdder octaladder_1 (.CarryIn(CarryIn), .A(A[7:0]), .B(B[7:0]), .CarryOut(octaladder_1_carryout), .SUM(SUM[7:0]));
  OctalAdder octaladder_2 (
    .CarryIn(octaladder_1_carryout), .A(A[15:8]), .B(B[15:8]), .CarryOut(octaladder_2_carryout),
    .SUM(SUM[15:8]));
  OctalAdder octaladder_3 (
    .CarryIn(octaladder_2_carryout), .A(A[23:16]), .B(B[23:16]), .CarryOut(octaladder_3_carryout),
    .SUM(SUM[23:16]));
  OctalAdder octaladder_4 (
    .CarryIn(octaladder_3_carryout), .A(A[31:24]), .B(B[31:24]), .CarryOut(CarryOut), .SUM(SUM[31:24]));
endmodule
