// Logisim project bog1.circ as structural Verilog: 3 circuits, main circuit main
module main (
);

  wire CLK;

  Clock clock_1 (.out(CLK));
  Registers registers_1 (.CLOCK(CLK));  // open: RESET, WRITE_EN, A_ADDR, B_ADDR, WRITE_ADDR, WRITE_DATA, A_DATA, B_DATA
endmodule

module Registers (
  input  CLOCK,
  input  RESET,
  input  WRITE_EN,
  input  [4:0] A_ADDR,
  input  [4:0] B_ADDR,
  input  [4:0] WRITE_ADDR,
  input  [31:0] WRITE_DATA,
  output [31:0] A_DATA,
  output [31:0] B_DATA
);

  wire CLK, R1_EN, R2_EN, R3_EN, R4_EN, R5_EN, R6_EN, R7_EN, R8_EN;
  wire [31:0] R1_IN, R1_OUT, R2_IN, R2_OUT, R3_IN, R3_OUT, R4_IN, R4_OUT, R5_IN, R5_OUT, R6_IN, R6_OUT,
       R7_IN, R7_OUT, R8_IN, R8_OUT;

  Register #(.width(32)) R1 (.D(R1_IN), .en(R1_EN), .clk(CLK), .Q(R1_OUT), .clr(RESET));
  Register #(.width(32)) R5 (.D(R5_IN), .en(R5_EN), .clk(CLK), .Q(R5_OUT), .clr(RESET));
  Register #(.width(32)) register_1 (.D(R1_IN), .en(R1_EN), .clk(CLK), .Q(R1_OUT), .clr(RESET));
  Register #(.width(32)) register_2 (.D(R1_IN), .en(R1_EN), .clk(CLK), .Q(R1_OUT), .clr(RESET));
  Register #(.width(32)) register_3 (.D(R1_IN), .en(R1_EN), .clk(CLK), .Q(R1_OUT), .clr(RESET));
  Register #(.width(32)) register_4 (.D(R1_IN), .en(R1_EN), .clk(CLK), .Q(R1_OUT), .clr(RESET));
  Register #(.width(32)) register_5 (.D(R1_IN), .en(R1_EN), .clk(CLK), .Q(R1_OUT), .clr(RESET));
  Register #(.width(32)) register_6 (.D(R1_IN), .en(R1_EN), .clk(CLK), .Q(R1_OUT), .clr(RESET));
  Register #(.width(32)) R2 (.D(R2_IN), .en(R2_EN), .clk(CLK), .Q(R2_OUT), .clr(RESET));
  Register #(.width(32)) R6 (.D(R6_IN), .en(R6_EN), .clk(CLK), .Q(R6_OUT), .clr(RESET));
  Register #(.width(32)) register_7 (.D(R1_IN), .en(R1_EN), .clk(CLK), .Q(R1_OUT), .clr(RESET));
  Register #(.width(32)) register_8 (.D(R1_IN), .en(R1_EN), .clk(CLK), .Q(R1_OUT), .clr(RESET));
  Register #(.width(32)) register_9 (.D(R1_IN), .en(R1_EN), .clk(CLK), .Q(R1_OUT), .clr(RESET));
  Register #(.width(32)) register_10 (.D(R1_IN), .en(R1_EN), .clk(CLK), .Q(R1_OUT), .clr(RESET));
  Register #(.width(32)) register_11 (.D(R1_IN), .en(R1_EN), .clk(CLK), .Q(R1_OUT), .clr(RESET));
  Register #(.width(32)) register_12 (.D(R1_IN), .en(R1_EN), .clk(CLK), .Q(R1_OUT), .clr(RESET));
  Register #(.width(32)) R3 (.D(R3_IN), .en(R3_EN), .clk(CLK), .Q(R3_OUT), .clr(RESET));
  Register #(.width(32)) R7 (.D(R7_IN), .en(R7_EN), .clk(CLK), .Q(R7_OUT), .clr(RESET));
  Register #(.width(32)) register_13 (.D(R1_IN), .en(R1_EN), .clk(CLK), .Q(R1_OUT), .clr(RESET));
  Register #(.width(32)) register_14 (.D(R1_IN), .en(R1_EN), .clk(CLK), .Q(R1_OUT), .clr(RESET));
  Register #(.width(32)) register_15 (.D(R1_IN), .en(R1_EN), .clk(CLK), .Q(R1_OUT), .clr(RESET));
  Register #(.width(32)) register_16 (.D(R1_IN), .en(R1_EN), .clk(CLK), .Q(R1_OUT), .clr(RESET));
  Register #(.width(32)) register_17 (.D(R1_IN), .en(R1_EN), .clk(CLK), .Q(R1_OUT), .clr(RESET));
  Register #(.width(32)) register_18 (.D(R1_IN), .en(R1_EN), .clk(CLK), .Q(R1_OUT), .clr(RESET));
  Register #(.width(32)) R4 (.D(R4_IN), .en(R4_EN), .clk(CLK), .Q(R4_OUT), .clr(RESET));
  Register #(.width(32)) R8 (.D(R8_IN), .en(R8_EN), .clk(CLK), .Q(R8_OUT), .clr(RESET));
  Register #(.width(32)) register_19 (.D(R1_IN), .en(R1_EN), .clk(CLK), .Q(R1_OUT), .clr(RESET));
  Register #(.width(32)) register_20 (.D(R1_IN), .en(R1_EN), .clk(CLK), .Q(R1_OUT), .clr(RESET));
  Register #(.width(32)) register_21 (.D(R1_IN), .en(R1_EN), .clk(CLK), .Q(R1_OUT), .clr(RESET));
  Register #(.width(32)) register_22 (.D(R1_IN), .en(R1_EN), .clk(CLK), .Q(R1_OUT), .clr(RESET));
  Register #(.width(32)) register_23 (.D(R1_IN), .en(R1_EN), .clk(CLK), .Q(R1_OUT), .clr(RESET));

  // Other names for the same wires on the sheet: REG_A_ADDR[4:0] = A_ADDR; REG_A_DATA[31:0] = A_DATA;
  //   REG_B_ADDR[4:0] = B_ADDR; REG_B_DATA[31:0] = B_DATA; REG_WRITE_ADDR[4:0] = WRITE_ADDR;
  //   REG_WRITE_DATA[31:0] = WRITE_DATA

  // Notes on the sheet:
  //   Pins
endmodule

module ALU (
);


  // Notes on the sheet:
  //   I/O
  //   Operations
endmodule
